# Fritzing sketch Stopwatch-receiver-schematic-diagram (saved by Fritzing 1.0.1rc)

parts:
  Disp1 = 38mm 8x8 dot matrix row cathode led display with narrow pcb pads  # not connected
  Disp2 = 38mm 8x8 dot matrix row cathode led display with narrow pcb pads  # not connected
  Disp3 = 38mm 8x8 dot matrix row cathode led display with narrow pcb pads  # not connected
  Disp4 = 38mm 8x8 dot matrix row cathode led display with narrow pcb pads  # not connected
  LCD1 = LCD screen  # not connected
  Part1 = Bluetooth HC-05 Macho
  HC-SR04_Sensor_1 = HC-SR04 Ultrasonic Distance Sensor
  S1 = Pushbutton [package="[THT]"]
  Part2 = Arduino Nano (Rev3.0) (ICSP)
  S2 = Pushbutton [package="[THT]"]
  S3 = Pushbutton [package="[THT]"]
  ANT1 = Antenna  # not connected
  C1 = Capacitor Polarized [package=cpol-radial-10uf-25v]
  R1 = Resistor [tolerance=±5% resistance=220 package="0402 [SMD]"]
  R2 = Resistor [tolerance=±5% resistance=220 package="0402 [SMD]"]
  R3 = Resistor [tolerance=±5% resistance=220 package="0402 [SMD]"]
  JP1 = Header 4 [package=molex-1x4_lock]
  JP2 = Header 5x2 [package=2x5-raf]

nets:
  N1: Part1.TXD, Part2.D0/RX
  N2: Part1.RXD, Part2.D1/TX
  VCC: Part1.VCC, HC-SR04_Sensor_1.VCC, Part2.5V, C1.+, R1.Pin_1, R2.Pin_1, R3.Pin_1, JP1.3, JP2.1
  GND: Part1.GND, HC-SR04_Sensor_1.GND, S1.Pin_1, Part2.GND, S2.Pin_1, S2.Pin_2, S3.Pin_1, S3.Pin_2, C1.-, JP1.4, JP2.3
  N3: HC-SR04_Sensor_1.TRIG, Part2.D9
  N4: HC-SR04_Sensor_1.ECHO, Part2.D8
  N5: S1.Pin_3, S1.Pin_4, Part2.D5, R1.Pin_0
  N6: Part2.D2, S3.Pin_3, S3.Pin_4, R3.Pin_0
  N7: Part2.D3, JP2.7
  N8: Part2.D4, S2.Pin_3, S2.Pin_4, R2.Pin_0
  N9: Part2.D11/MOSI, JP2.5
  N10: Part2.A5, JP1.1
  N11: Part2.A4, JP1.2
  N12: Part2.D13/SCK, JP2.9

notes:
  HC-12*
