# Fritzing sketch Stopwatch-transmitter-schematic-diagram (saved by Fritzing 1.0.1rc)

parts:
  Part3 = Arduino Nano (Rev3.0) (ICSP)
  Part4 = Bluetooth HC-05 Macho
  ANT2 = Antenna  # not connected
  HC-SR04_Sensor_2 = HC-SR04 Ultrasonic Distance Sensor
  S4 = Pushbutton [package="[THT]"]
  LED1 = LED - 5mm [color="Red (633nm)" current=0.030A package="5 mm [THT]"]
  R2 = Resistor [tolerance=±5% resistance=220 package="0402 [SMD]"]
  C2 = Capacitor Polarized [package=cpol-radial-10uf-25v]
  R3 = Resistor [tolerance=±5% resistance=220 package="0402 [SMD]"]

nets:
  N1: Part3.D1/TX, Part4.TXD
  N2: Part3.D0/RX, Part4.RXD
  N3: Part3.D2, R3.Pin_1
  N4: Part3.D3, Part4.Key, S4.Pin_3, S4.Pin_4, R2.Pin_0
  N5: Part3.D8, HC-SR04_Sensor_2.ECHO
  N6: Part3.D9, HC-SR04_Sensor_2.TRIG
  GND: Part3.GND, Part4.GND, HC-SR04_Sensor_2.GND, S4.Pin_1, S4.Pin_2, LED1.cathode, C2.-
  VCC: Part3.5V, Part3.A7, Part4.VCC, HC-SR04_Sensor_2.VCC, R2.Pin_1, C2.+
  N7: LED1.anode, R3.Pin_0

notes:
  HC-12*
